# Fritzing sketch Raspi Controller (saved by Fritzing 0.9.1b)

parts:
  Raspberry_Pi1 = Raspberry Pi B+
  U2 = XBEE-1 [package=xbee-1_lock]

nets:
  3V3: Raspberry_Pi1.3v3, Raspberry_Pi1.3V3, U2.VDD
  GND: Raspberry_Pi1.GND, U2.GND
  N1: Raspberry_Pi1.GPIO15, U2.DOUT
  N2: Raspberry_Pi1.GPIO14, U2.DIN
