# Fritzing sketch Sign (saved by Fritzing 0.9.1b)

parts:
  Part1 = Arduino Mega 2560 (Rev3)  # not connected
  Segment_1_Femtobuck = femtobuck
  LED2 = LED - 3W Aluminum PCB
  LED3 = LED - 3W Aluminum PCB
  LED4 = LED - 3W Aluminum PCB
  LED5 = LED - 3W Aluminum PCB
  LED6 = LED - 3W Aluminum PCB
  LED7 = LED - 3W Aluminum PCB
  XBee_Shield = Arduino XBee Shield
  Segment_2_Femtobuck = femtobuck
  LED8 = LED - 3W Aluminum PCB
  LED9 = LED - 3W Aluminum PCB
  LED10 = LED - 3W Aluminum PCB
  LED11 = LED - 3W Aluminum PCB
  LED12 = LED - 3W Aluminum PCB
  LED13 = LED - 3W Aluminum PCB
  Segment_3_Femtobuck = femtobuck
  LED14 = LED - 3W Aluminum PCB
  LED15 = LED - 3W Aluminum PCB
  LED16 = LED - 3W Aluminum PCB
  LED17 = LED - 3W Aluminum PCB
  LED18 = LED - 3W Aluminum PCB
  LED19 = LED - 3W Aluminum PCB
  Segment_4_Femtobuck = femtobuck
  LED20 = LED - 3W Aluminum PCB
  LED21 = LED - 3W Aluminum PCB
  LED22 = LED - 3W Aluminum PCB
  LED23 = LED - 3W Aluminum PCB
  LED24 = LED - 3W Aluminum PCB
  LED25 = LED - 3W Aluminum PCB
  Segment_5_Femtobuck = femtobuck
  LED26 = LED - 3W Aluminum PCB
  LED27 = LED - 3W Aluminum PCB
  LED28 = LED - 3W Aluminum PCB
  LED29 = LED - 3W Aluminum PCB
  LED30 = LED - 3W Aluminum PCB
  LED31 = LED - 3W Aluminum PCB
  Segment_6_Femtobuck = femtobuck
  LED32 = LED - 3W Aluminum PCB
  LED33 = LED - 3W Aluminum PCB
  LED34 = LED - 3W Aluminum PCB
  LED35 = LED - 3W Aluminum PCB
  LED36 = LED - 3W Aluminum PCB
  LED37 = LED - 3W Aluminum PCB
  Segment_7_Femtobuck = femtobuck
  LED38 = LED - 3W Aluminum PCB
  LED39 = LED - 3W Aluminum PCB
  LED40 = LED - 3W Aluminum PCB
  LED41 = LED - 3W Aluminum PCB
  LED42 = LED - 3W Aluminum PCB
  LED43 = LED - 3W Aluminum PCB
  Segment_8_Femtobuck = femtobuck
  LED44 = LED - 3W Aluminum PCB
  LED45 = LED - 3W Aluminum PCB
  LED46 = LED - 3W Aluminum PCB
  LED47 = LED - 3W Aluminum PCB
  LED48 = LED - 3W Aluminum PCB
  LED49 = LED - 3W Aluminum PCB
  Power_plug1 = Power plug
  U1 = XBee  # not connected

nets:
  GND: Segment_1_Femtobuck.V-, XBee_Shield.GND, Segment_2_Femtobuck.V-, Segment_3_Femtobuck.V-, Segment_4_Femtobuck.V-, Segment_5_Femtobuck.V-, Segment_6_Femtobuck.V-, Segment_7_Femtobuck.V-, Segment_8_Femtobuck.V-, Power_plug1.GND
  12V: Segment_1_Femtobuck.V+, XBee_Shield.VIN, Segment_2_Femtobuck.V+, Segment_3_Femtobuck.V+, Segment_4_Femtobuck.V+, Segment_5_Femtobuck.V+, Segment_6_Femtobuck.V+, Segment_7_Femtobuck.V+, Segment_8_Femtobuck.V+, Power_plug1.VCC
  N1: Segment_1_Femtobuck.D+, XBee_Shield.D_RX
  N2: Segment_1_Femtobuck.LED-, LED6.cathode, LED7.cathode
  N3: Segment_1_Femtobuck.LED+, LED2.anode, LED3.anode
  N4: LED2.cathode, LED5.anode
  N5: LED3.cathode, LED4.anode
  N6: LED4.cathode, LED6.anode
  N7: LED5.cathode, LED7.anode
  N8: XBee_Shield.D_TX, Segment_2_Femtobuck.D+
  N9: XBee_Shield.D4, Segment_3_Femtobuck.D+
  N10: XBee_Shield.D5, Segment_4_Femtobuck.D+
  N11: XBee_Shield.D6, Segment_5_Femtobuck.D+
  N12: XBee_Shield.D7, Segment_6_Femtobuck.D+
  N13: XBee_Shield.D9, Segment_8_Femtobuck.D+
  N14: XBee_Shield.D8, Segment_7_Femtobuck.D+
  N15: Segment_2_Femtobuck.LED-, LED9.cathode, LED13.cathode
  N16: Segment_2_Femtobuck.LED+, LED8.anode, LED11.anode
  N17: LED8.cathode, LED12.anode
  N18: LED9.anode, LED12.cathode
  N19: LED10.anode, LED11.cathode
  N20: LED10.cathode, LED13.anode
  N21: Segment_3_Femtobuck.LED-, LED15.cathode, LED18.cathode
  N22: Segment_3_Femtobuck.LED+, LED17.anode, LED19.anode
  N23: LED14.anode, LED17.cathode
  N24: LED14.cathode, LED18.anode
  N25: LED15.anode, LED16.cathode
  N26: LED16.anode, LED19.cathode
  N27: Segment_4_Femtobuck.LED-, LED21.cathode, LED25.cathode
  N28: Segment_4_Femtobuck.LED+, LED20.anode, LED22.anode
  N29: LED20.cathode, LED24.anode
  N30: LED21.anode, LED24.cathode
  N31: LED22.cathode, LED23.anode
  N32: LED23.cathode, LED25.anode
  N33: Segment_5_Femtobuck.LED-, LED26.cathode, LED28.cathode
  N34: Segment_5_Femtobuck.LED+, LED29.anode, LED31.anode
  N35: LED26.anode, LED30.cathode
  N36: LED27.anode, LED29.cathode
  N37: LED27.cathode, LED28.anode
  N38: LED30.anode, LED31.cathode
  N39: Segment_6_Femtobuck.LED-, LED32.cathode, LED34.cathode
  N40: Segment_6_Femtobuck.LED+, LED35.anode, LED36.anode
  N41: LED32.anode, LED37.cathode
  N42: LED33.anode, LED36.cathode
  N43: LED33.cathode, LED34.anode
  N44: LED35.cathode, LED37.anode
  N45: Segment_7_Femtobuck.LED-, LED38.cathode, LED42.cathode
  N46: Segment_7_Femtobuck.LED+, LED39.anode, LED40.anode
  N47: LED38.anode, LED43.cathode
  N48: LED39.cathode, LED41.anode
  N49: LED40.cathode, LED43.anode
  N50: LED41.cathode, LED42.anode
  N51: Segment_8_Femtobuck.LED-, LED47.cathode, LED49.cathode
  N52: Segment_8_Femtobuck.LED+, LED44.anode, LED46.anode
  N53: LED44.cathode, LED45.anode
  N54: LED45.cathode, LED47.anode
  N55: LED46.cathode, LED48.anode
  N56: LED48.cathode, LED49.anode

notes:
  Make sure this switch is set to "UART" when using the XBee, and "DLINE" when controlling the Arduino viaUSB

custom parts:
  femtobuck: Description: This is the FemtoBuck, a small-size single-output constant current LED driver. Each FemtoBuck has the capability to dim a single high-power channel of LEDs from 0-350mA at up to 36V while the dimming control can be either accessed via PWM or analog signal from 0-2.5V. This board is based off of the PicoBuck LED Driver, developed in collaboration with Ethan Zonca, except instead of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
  LED - 3W Aluminum PCB: Description: So much power and light from such a small package. This 5 pack of red 3 Watt aluminum backed PCBs is sure to shed a lot of light on any project you add it to. These LEDs act as any other LED except these little guys require much more power while delivering a light as intense of a thousand suns going super nova (this is an exaggeration but you know what we mean)! Each LED in the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
