# Fritzing sketch Single Segment Test (saved by Fritzing 0.9.0b)
breadboards: 1

parts:
  LED1 = LED - 5mm [color="Red (633nm)" current=70mA package="5 mm [THT]"]
  LED2 = LED - 5mm [color="Red (633nm)" package="5 mm [THT]"]
  LED3 = LED - 5mm [color="Red (633nm)" package="5 mm [THT]"]
  LED4 = LED - 5mm [color="Red (633nm)" package="5 mm [THT]"]
  LED6 = LED - 5mm [color="Red (633nm)" package="5 mm [THT]"]
  R1 = Resistor [tolerance=±5% resistance=10 package=THT]
  R2 = Resistor [tolerance=±5% resistance=10 package=THT]
  LED5 = LED - 5mm [color="Red (633nm)" package="5 mm [THT]"]
  R3 = Resistor [tolerance=±5% resistance=10 package=THT]
  Q1 = NPN-Transistor [package="TO92 [THT]"]

nets:
  N1: LED1.cathode, LED2.anode
  5V: LED1.anode, LED3.anode, LED5.anode
  N2: LED2.cathode, R1.Pin_1
  N3: LED3.cathode, LED6.anode
  N4: LED4.cathode, R3.Pin_1
  N5: LED4.anode, LED5.cathode
  N6: LED6.cathode, R2.Pin_1
  N7: R1.Pin_0, R2.Pin_0, R3.Pin_0, Q1.C
  GND: Q1.E
